# Fritzing sketch rover_num5 (saved by Fritzing 0.8.7b)
breadboards: 1

parts:
  Parte1 = Dual H-Bridge L298
  Parte2 = Arduino Uno (Rev3)
  M1 = DC Motor
  M2 = DC Motor
  M3 = DC Motor
  M4 = DC Motor
  J1 = Basic Servo
  U2 = HC-SR04 [chip_label=IC package="SIP (Single Inline) [THT]"]
  S1 = Toggle Switch [package=THT]
  Parte3 = JY-MCU

nets:
  N1: Parte1.MOTORA1, M2.pin_2, M4.pin_2
  N2: Parte1.MOTORA2, M2.pin_1, M4.pin_1
  N3: Parte1.VMS, Parte2.VIN
  GND: Parte1.GND, Parte2.GND, J1.gnd, U2.GND, S1.COM, Parte3.GND
  N4: Parte1.MOTORB1, M1.pin_1, M3.pin_1
  N5: Parte1.MOTORB2, M1.pin_2, M3.pin_2
  N6: Parte1.ENA, Parte2.D6_PWM
  N7: Parte1.IN1, Parte2.D5_PWM
  N8: Parte1.IN2, Parte2.D7
  N9: Parte1.IN3, Parte2.D4
  N10: Parte1.IN4, Parte2.D2
  N11: Parte1.ENB, Parte2.D3_PWM
  N12: Parte2.A0, Parte3.TX
  N13: Parte2.A1, Parte3.RX
  N14: Parte2.D8, S1.L1
  N15: Parte2.D10_PWM/SS, J1.pulse
  N16: Parte2.D11_PWM/MOSI, U2.Echo
  N17: Parte2.D12/MISO, U2.Trig
  VCC: Parte2.5V, J1.vcc, U2.Vcc, Parte3.VCC

notes:
  Default Mode
  BT
  Automatic
  ArduBlueBot v.1.0

custom parts:
  Dual H-Bridge L298: Description:The L298N driver module, using ST's L298N chip can directly drive two 3-30V DC motor, and provides a 5V output interface can 5V single-chip circuitry to supply, support 3.3VMCU control, you can easily control the DC motor speed and direction, you can also control the 2-phase stepper motor, smart car essential. Features: Driver: L298N Dual H Bridge DC Motor Driver IC Driven part of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
  HC-SR04: HC-SR04 ultrasound distance sensor
  JY-MCU: Description: The Bluetooth Mate is very similar to our BlueSMiRF modem, but it is designed specifically to be used with our Arduino Pros and LilyPad Arduinos. These modems work as a serial (RX/TX) pipe, and are a great wireless replacement for serial cables. Any serial stream from 9600 to 115200bps can be passed seamlessly from your computer to your target. Bluetooth Mate has the same pin out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
